// Logisim project cpu.circ as structural Verilog: 1 circuit, main circuit CPU
module CPU (
  input  [31:0] Instruction,
  input  CLK,
  output [31:0] s0,
  output [31:0] s1,
  output [31:0] t0,
  output [31:0] t1,
  output [31:0] a0,
  output [31:0] ra,
  output [31:0] sp,
  output [31:0] PC
);

  wire undriven;
  wire [31:0] alu_1_out, incrementer_1_p1, instruction_t, itype, itype_ls, jalr, rtype, sbtype, stype,
       ujtype, utype;

  // Incrementer incrementer_1: pin names not known; wires that end beside it: incrementer_1_p1
  PC pc_1 (.Input(incrementer_1_p1), .Clk(CLK));  // open: Output
  RegFile regfile_1 (.Clk(CLK));  // open: R1, R2, WE, W, RD, RS1, RS2, s0, s1, t0, t1, a0, ra, sp
  Demultiplexer #(.select(5), .width(32)) demultiplexer_1 (
    .out0(itype_ls), .out4(itype), .out8(stype), .out12(rtype), .out13(utype), .out24(sbtype), .out25(jalr),
    .out27(ujtype), .in(instruction_t), .sel(instruction_t[6:2]));  // open: out1, out2, out3, out5, out6, out7, out9, out10, out11, out14, out15, out16, out17, out18, out19, out20, out21, out22, out23, out26, out28, out29, out30, out31, en
  ALU alu_1 (.Out(alu_1_out));  // open: A, B, ALU_Op, Equal, LT, LTU
  memory_main main_1 (.WE(undriven), .Data(alu_1_out), .Clk(CLK));  // open: Address, Out

  // Other names for the same wires on the sheet: fetch_addr[31:0] = PC; INST[31:0] = Instruction;
  //   opcode[4:0] = instruction_t[6:2]

  // Notes on the sheet:
  //   0 (top) bits 2-6: opcode
  //   1: bits 12-14 func3
  //   2: bits 25-31 func7
  //   NOTE
  //   Please do not modify/replace/move/change/delete/etc input and output pins
  //   3(bottom: Don't care for instruction routing.
  //   00100xx: 4
  //   01000xx:  8
  //   01100xx: 12
  //   01101xx: 13
  //   00000xx: 0
  //   11000xx: 24
  //   11001xx: 25
  //   11011xx: 27
  //   These are debug/test outputs from your circuit
endmodule
